# Fritzing sketch joystick (saved by Fritzing 0.9.3b)
breadboards: 1

parts:
  Componente1 = Arduino Uno (Rev3)
  Componente2 = LED Matrix - Serial Interface - Red/Green/Blue
  Componente3 = Thumb Joystick

nets:
  N1: Componente1.A0, Componente3.HORZ
  N2: Componente1.A1, Componente3.VERT
  N3: Componente1.D8, Componente3.SEL
  N4: Componente1.D3_PWM, Componente2.CS
  N5: Componente1.D4, Componente2.SCK
  N6: Componente1.D5_PWM, Componente2.MOSI
  VCC: Componente1.5V, Componente2.VCC, Componente3.VCC
  GND: Componente1.GND, Componente2.GND, Componente3.GND
